# Fritzing sketch circuit (saved by Fritzing 0.9.3b)
breadboards: 1

parts:
  U1 = TA7291P [package=HSIP10-P-2.54(THT)]
  U2 = TA7291P [package=HSIP10-P-2.54(THT)]
  M1 = DC Motor
  M2 = DC Motor
  VCC1 = Battery block 9V
  パーツ1 = Arduino Uno (Rev3)
  GY1 = MPU-6050 Board GY-521 [form="♀ (female)" package=THT]
  S1 = Momentary Switch [package=ksa_sealed_tac_switch]

nets:
  GND: U1.GND, U2.GND, VCC1.-, パーツ1.GND, GY1.pin2, S1.2
  N1: U1.OUT1, M2.pin_1
  VCC: U1.Vref, U1.Vcc, U2.Vref, U2.Vcc, パーツ1.5V, GY1.pin1
  N2: U1.IN1, パーツ1.D10_PWM/SS
  N3: U1.IN2, パーツ1.D11_PWM/MOSI
  N4: U1.Vs, U2.Vs, VCC1.+
  N5: U1.OUT2, M2.pin_2
  N6: U2.OUT1, M1.pin_1
  N7: U2.IN1, パーツ1.D5_PWM
  N8: U2.IN2, パーツ1.D6_PWM
  N9: U2.OUT2, M1.pin_2
  N10: パーツ1.A4/SDA, GY1.pin4
  N11: パーツ1.A5/SCL, GY1.pin3
  N12: パーツ1.D2, S1.4

custom parts:
  TA7291P: The IC are Full-Bridge Driver. 4 modes available (CW / CCW / STOP / BRAKE) and PWM control. Output current:1.0 A (AVE.) 2.0 A (PEAK)
  MPU-6050 Board GY-521: Acelerometro y Giroscopio MPU-6050 Board GY-521
